// Logisim project ALU_circuit_design_with_full_adder.circ as structural Verilog: 3 circuits, main circuit main
module main (
  input  C_in,
  input  S0,
  input  S1,
  input  B0,
  input  A0,
  input  A1,
  input  B1,
  input  A2,
  input  B2,
  input  A3,
  input  A4,
  input  B3,
  input  A5,
  input  B4,
  input  A6,
  input  B5,
  input  A7,
  input  B6,
  input  B7,
  output F0,
  output F1,
  output F2,
  output F3,
  output F4,
  output F5,
  output F6,
  output F7,
  output C_OUT
);

  wire adder_1_c, adder_2_c, adder_3_c, adder_4_c, adder_5_c, adder_6_c, adder_7_c, and_1_out, and_2_out,
       and_3_out, and_4_out, and_5_out, and_6_out, and_7_out, and_8_out, and_9_out, and_10_out, and_11_out,
       and_12_out, and_13_out, and_14_out, and_15_out, and_16_out, not_1_out, not_2_out, not_3_out,
       not_4_out, not_5_out, not_6_out, not_7_out, not_8_out, or_1_out, or_2_out, or_3_out, or_4_out,
       or_5_out, or_6_out, or_7_out, or_8_out;

  not not_1 (not_1_out, B0);
  not not_2 (not_2_out, B1);
  not not_3 (not_3_out, B2);
  not not_4 (not_4_out, B3);
  not not_5 (not_5_out, B4);
  not not_6 (not_6_out, B5);
  not not_7 (not_7_out, B6);
  not not_8 (not_8_out, B7);
  and and_1 (and_1_out, B0, S0);
  and and_2 (and_2_out, not_1_out, S1);
  and and_3 (and_3_out, B1, S0);
  and and_4 (and_4_out, not_2_out, S1);
  and and_5 (and_5_out, B2, S0);
  and and_6 (and_6_out, not_3_out, S1);
  and and_7 (and_7_out, B3, S0);
  and and_8 (and_8_out, not_4_out, S1);
  and and_9 (and_9_out, B4, S0);
  and and_10 (and_10_out, not_5_out, S1);
  and and_11 (and_11_out, B5, S0);
  and and_12 (and_12_out, not_6_out, S1);
  and and_13 (and_13_out, B6, S0);
  and and_14 (and_14_out, not_7_out, S1);
  and and_15 (and_15_out, B7, S0);
  and and_16 (and_16_out, not_8_out, S1);
  or or_1 (or_1_out, and_1_out, and_2_out);
  or or_2 (or_2_out, and_3_out, and_4_out);
  or or_3 (or_3_out, and_5_out, and_6_out);
  or or_4 (or_4_out, and_7_out, and_8_out);
  or or_5 (or_5_out, and_9_out, and_10_out);
  or or_6 (or_6_out, and_11_out, and_12_out);
  or or_7 (or_7_out, and_13_out, and_14_out);
  or or_8 (or_8_out, and_15_out, and_16_out);
  adder adder_1 (.X(A0), .Y(or_1_out), .Z(C_in), .S(F0), .C(adder_1_c));
  adder adder_2 (.X(A2), .Y(or_3_out), .Z(adder_5_c), .S(F2), .C(adder_2_c));
  adder adder_3 (.X(A4), .Y(or_5_out), .Z(adder_6_c), .S(F4), .C(adder_3_c));
  adder adder_4 (.X(A6), .Y(or_7_out), .Z(adder_7_c), .S(F6), .C(adder_4_c));
  adder adder_5 (.X(A1), .Y(or_2_out), .Z(adder_1_c), .S(F1), .C(adder_5_c));
  adder adder_6 (.X(A3), .Y(or_4_out), .Z(adder_2_c), .S(F3), .C(adder_6_c));
  adder adder_7 (.X(A5), .Y(or_6_out), .Z(adder_3_c), .S(F5), .C(adder_7_c));
  adder adder_8 (.X(A7), .Y(or_8_out), .Z(adder_4_c), .S(F7), .C(C_OUT));

  // Notes on the sheet:
  //   1607022
  //   A=2 , B=2 
  //   Binary = 01 
  //   A0=0,A1=1
  //   B0=0,B1=1
endmodule

// F Ad
module adder (
  input  X,
  input  Y,
  input  Z,
  output S,
  output C
);

  wire and_1_out, and_2_out, xor_1_out;

  xor xor_1 (xor_1_out, X, Y);
  and and_1 (and_1_out, X, Y);
  and and_2 (and_2_out, xor_1_out, Z);
  xor xor_2 (S, xor_1_out, Z);
  or or_1 (C, and_2_out, and_1_out);

  // Notes on the sheet:
  //   1607022
endmodule

// TC
module _2_s_compliment (
  input  IN_S0,
  input  IN_S1,
  input  IN_B,
  output OUT_B
);

  wire and_1_out, and_2_out, not_1_out;

  not not_1 (not_1_out, IN_B);
  and and_1 (and_1_out, IN_B, IN_S0);
  buf and_2 (and_2_out, IN_S1);  // AND_Gate
  or or_1 (OUT_B, and_1_out, and_2_out);

  // Notes on the sheet:
  //   1607022
endmodule
