// Logisim project ALU_design_logic_operation.circ as structural Verilog: 3 circuits, main circuit main
module main (
  input  C_IN,
  input  S0,
  input  S1,
  input  S2,
  input  A0,
  input  B0,
  input  A1,
  input  B1,
  input  A2,
  input  B2,
  input  A3,
  input  B3,
  output F0,
  output F1,
  output F2,
  output F3,
  output C_OUT
);

  wire adder_1_c, adder_2_c, adder_3_c, adder_4_c, and_1_out, and_2_out, and_3_out, and_4_out, and_5_out,
       and_6_out, and_7_out, and_8_out, and_9_out, and_10_out, and_11_out, and_12_out, and_13_out,
       and_14_out, not_1_out, not_2_out, not_3_out, not_4_out, not_5_out, not_6_out, not_7_out, or_1_out,
       or_2_out, or_3_out, or_4_out, part1_1_y, part1_2_y, part1_3_y, part1_4_y;

  not not_1 (not_1_out, B0);
  not not_2 (not_2_out, S2);
  not not_3 (not_3_out, B1);
  not not_4 (not_4_out, B2);
  not not_5 (not_5_out, B3);
  and and_1 (and_1_out, B1, S0);
  and and_2 (and_2_out, not_3_out, S1);
  and and_3 (and_3_out, B2, S0);
  and and_4 (and_4_out, not_4_out, S1);
  and and_5 (and_5_out, B3, S0);
  and and_6 (and_6_out, not_5_out, S1);
  or or_1 (or_1_out, and_1_out, and_2_out);
  or or_2 (or_2_out, and_3_out, and_4_out);
  or or_3 (or_3_out, and_5_out, and_6_out);
  not not_6 (not_6_out, S0);
  and and_7 (and_7_out, not_6_out, S1, S2);
  not not_7 (not_7_out, S1);
  and and_8 (and_8_out, not_6_out, not_7_out, S2);
  and and_9 (and_9_out, B0, S0);
  and and_10 (and_10_out, not_1_out, S1);
  PART1 part1_1 (._1ST(and_8_out), ._2ND_b(B2), ._3RD(and_7_out), ._4TH_b_not(not_4_out), .A(A2), .Y(part1_1_y));
  PART1 part1_2 (._1ST(and_8_out), ._2ND_b(B3), ._3RD(and_7_out), ._4TH_b_not(not_5_out), .A(A3), .Y(part1_2_y));
  and and_11 (and_11_out, C_IN, not_2_out);
  PART1 part1_3 (._1ST(and_8_out), ._2ND_b(B1), ._3RD(and_7_out), ._4TH_b_not(not_3_out), .A(A1), .Y(part1_3_y));
  PART1 part1_4 (._1ST(and_8_out), ._2ND_b(B0), ._3RD(and_7_out), ._4TH_b_not(not_1_out), .A(A0), .Y(part1_4_y));
  or or_4 (or_4_out, and_9_out, and_10_out);
  adder adder_1 (.X(part1_4_y), .Y(or_4_out), .Z(and_11_out), .S(F0), .C(adder_1_c));
  and and_12 (and_12_out, not_2_out, adder_1_c);
  adder adder_2 (.X(part1_3_y), .Y(or_1_out), .Z(and_12_out), .S(F1), .C(adder_2_c));
  and and_13 (and_13_out, not_2_out, adder_2_c);
  adder adder_3 (.X(part1_1_y), .Y(or_2_out), .Z(and_13_out), .S(F2), .C(adder_3_c));
  and and_14 (and_14_out, not_2_out, adder_3_c);
  adder adder_4 (.X(part1_2_y), .Y(or_3_out), .Z(and_14_out), .S(F3), .C(adder_4_c));
  and and_15 (C_OUT, not_2_out, adder_4_c);

  // Notes on the sheet:
  //   1607022
endmodule

// FA
module adder (
  input  X,
  input  Y,
  input  Z,
  output S,
  output C
);

  wire and_1_out, and_2_out, xor_1_out;

  xor xor_1 (xor_1_out, X, Y);
  and and_1 (and_1_out, X, Y);
  xor xor_2 (S, xor_1_out, Z);
  and and_2 (and_2_out, xor_1_out, Z);
  or or_1 (C, and_2_out, and_1_out);

  // Notes on the sheet:
  //   1607022
endmodule

// P1
module PART1 (
  input  _1ST,
  input  _2ND_b,
  input  _3RD,
  input  _4TH_b_not,
  input  A,
  output Y
);

  wire and_1_out, and_2_out;

  and and_1 (and_1_out, _1ST, _2ND_b);
  and and_2 (and_2_out, _3RD, _4TH_b_not);
  ExactlyOne xor_1 (.out(Y), .in0(and_1_out), .in1(and_2_out), .in2(A));

  // Notes on the sheet:
  //   1607022
endmodule
