// Logisim project DSD_register_connection_bus.circ as structural Verilog
module buffer_register (
  input  X3,
  input  X,
  input  X1,
  input  X0,
  input  LOAD,
  input  Clear,
  input  Enable,
  output Y3,
  output Y2,
  output Y1,
  output Y0
);

  wire and_1_out, and_2_out, and_3_out, and_4_out, and_5_out, and_6_out, and_7_out, and_8_out, CLCK_out,
       d_ff_1_q, d_ff_2_q, d_ff_3_q, d_ff_4_q, not_1_out, or_1_out, or_2_out, or_3_out, or_4_out;

  and and_1 (and_1_out, d_ff_1_q, not_1_out);
  and and_2 (and_2_out, X3, LOAD);
  or or_1 (or_1_out, and_1_out, and_2_out);
  D_Flip_Flop d_ff_1 (.clk(CLCK_out), .D(or_1_out), .Q(d_ff_1_q), .reset(Clear));  // open: Qn, preset, en
  assign Y3 = Enable ? d_ff_1_q : 1'bz;  // Controlled_Buffer controlled_buffer_1
  and and_3 (and_3_out, d_ff_2_q, not_1_out);
  and and_4 (and_4_out, X, LOAD);
  or or_2 (or_2_out, and_3_out, and_4_out);
  D_Flip_Flop d_ff_2 (.clk(CLCK_out), .D(or_2_out), .Q(d_ff_2_q), .reset(Clear));  // open: Qn, preset, en
  assign Y2 = Enable ? d_ff_2_q : 1'bz;  // Controlled_Buffer controlled_buffer_2
  and and_5 (and_5_out, d_ff_3_q, not_1_out);
  or or_3 (or_3_out, and_5_out, and_6_out);
  and and_6 (and_6_out, X1, LOAD);
  D_Flip_Flop d_ff_3 (.clk(CLCK_out), .D(or_3_out), .Q(d_ff_3_q), .reset(Clear));  // open: Qn, preset, en
  assign Y1 = Enable ? d_ff_3_q : 1'bz;  // Controlled_Buffer controlled_buffer_3
  and and_7 (and_7_out, X0, LOAD);
  and and_8 (and_8_out, d_ff_4_q, not_1_out);
  or or_4 (or_4_out, and_8_out, and_7_out);
  D_Flip_Flop d_ff_4 (.clk(CLCK_out), .D(or_4_out), .Q(d_ff_4_q), .reset(Clear));  // open: Qn, preset, en
  assign Y0 = Enable ? d_ff_4_q : 1'bz;  // Controlled_Buffer controlled_buffer_4
  not not_1 (not_1_out, LOAD);
  Clock CLCK (.out(CLCK_out));

  // Notes on the sheet:
  //   1607022
endmodule
